# Fritzing sketch ESP8266BB (saved by Fritzing 0.9.2b)
circuit board: 8.46667cm x 5.64cm
breadboards: 1

parts:
  U3 = ESP8266 WiFi Module [part_number=ESP8266]
  U4 = Voltage Regulator - 5V [package="TO220 [THT]"]
  C1 = Electrolytic Capacitor [capacitance=0.1µF package="100 mil [THT, electrolytic]"]
  C2 = Electrolytic Capacitor [capacitance=2.2µF package="100 mil [THT, electrolytic]"]
  J1 = female pin header, 2 pins [form="♀ (female)" part_number=fdgdfg]
  J2 = female pin header, 2 pins [form="♀ (female)"]
  J3 = female pin header, 4 pins [form="♀ (female)"]
  J4 = female pin header, 8 pins [form="♀ (female)"]

nets:
  N1: U3.RXD, J4.pin6
  N2: U3.VCC, U4.output_voltage, C2.+, J4.pin3
  N3: U3.GPIO_0, J1.pin1, J4.pin5
  N4: U3.GPIO_2, J4.pin4
  GND: U3.GND, U4.GND, C1.-, C2.-, J1.pin2, J2.pin1, J3.pin1, J4.pin1
  N5: U3.TXD, J4.pin7
  N6: U4.input_voltage, C1.+, J2.pin2, J3.pin4, J4.pin2

custom parts:
  ESP8266 WiFi Module: Generic WiFi Module based on the ESP8266 with onboard PCB antenna and UART communications
